# Fritzing sketch Jetson Nano with LED and Transistor (saved by Fritzing 0.9.9b)
breadboards: 1

parts:
  Jetson_Nano2 = jetsonnano
  R1 = Resistor [tolerance=±1% power=0.25 resistance=270 package=THT]
  R3 = Resistor [tolerance=±1% power=0.25 resistance=47k package=THT]
  Q1 = NPN-Transistor [part_number=BC547 package="TO92 [THT]"]
  LED1 = LED - 3mm [color="Red (633nm)" current=0.030 package="3 mm [THT]"]

nets:
  N1: Jetson_Nano2.connector19, LED1.anode
  N2: Jetson_Nano2.connector22, Q1.C
  N3: R1.Pin_0, LED1.cathode
  N4: R1.Pin_1, Q1.E
  N5: R3.Pin_1, Q1.B
